// Logisim project main.circ as structural Verilog: 2 circuits, main circuit main
module main (
);

  wire half_adder_1_c, half_adder_1_s, switch_1_p2, switch_2_p2;

  // Switch switch_1: pin names not known; wires that end beside it: 1'b1, switch_1_p2
  // Switch switch_2: pin names not known; wires that end beside it: 1'b1, switch_2_p2
  half_adder half_adder_1 (.A(switch_1_p2), .B(switch_2_p2), .C(half_adder_1_c), .S(half_adder_1_s));
  LED led_1 (.in(half_adder_1_s));
  LED led_2 (.in(half_adder_1_c));
endmodule

// HA
module half_adder (
  input  A,
  input  B,
  output S,
  output C
);

  xor xor_1 (S, B, A);
  and and_1 (C, A, B);
endmodule
